# Fritzing sketch MowerSchematic (saved by Fritzing 0.9.3b)
breadboards: 1

parts:
  40a_breaker = FUSE [package=fuse_5mm]
  battery_1 = DC Power [voltage=12V]
  battery_2 = DC Power [voltage=12V]
  battery_3 = DC Power [voltage=12V]
  battery_4 = DC Power [voltage=12V]
  Cutter = DC Motor
  Left_wheel = DC Motor
  Right_wheel = DC Motor
  RELAY2 = CAR RELAY [part_number=NVF4-2 package=THT]
  U1 = RELAY [package=relay-t9a-2]  # not connected
  12to24Control = RELAY [package=relay-t9a]
  RELAY1 = CAR RELAY [part_number=NVF4-2 package=THT]
  RELAY3 = CAR RELAY [part_number=NVF4-2 package=THT]
  IC1 = H-Bridge [package=THT]
  20a_breaker1 = FUSE [package=fuse_5mm]
  20a_breaker2 = FUSE [package=fuse_5mm]

nets:
  N1: 40a_breaker.1, battery_4.V+, RELAY1.87A
  N2: 40a_breaker.2, Cutter.pin_2
  N3: battery_1.V+, battery_2.V+, 12to24Control.MAIN, RELAY1.86, RELAY3.30, IC1.VCC2, IC1.VCC1
  GND1: battery_1.V-, battery_2.V-, battery_3.V-, Cutter.pin_1, RELAY2.85, RELAY2.30, IC1.GND1, IC1.GND2
  N4: battery_3.V+, RELAY1.30, RELAY3.87A
  N5: battery_4.V-, RELAY2.87A, RELAY1.87
  N6: Left_wheel.pin_1, 20a_breaker1.2
  N7: Left_wheel.pin_2, IC1.2Y
  N8: Right_wheel.pin_1, 20a_breaker2.1
  N9: Right_wheel.pin_2, IC1.3Y
  N10: RELAY2.86, RELAY3.85
  N11: RELAY2.87, RELAY1.85
  N12: 12to24Control.NO, RELAY3.86
  N13: IC1.1Y, 20a_breaker1.1
  GND3: IC1.GND3, IC1.GND4
  N14: IC1.4Y, 20a_breaker2.2
